// Logisim project Adders.circ as structural Verilog
module HalfAdder (
  input  in_1,
  input  in_2,
  output out_3,
  output out_4
);

  xor xor_1 (out_3, in_1, in_2);
  and and_1 (out_4, in_1, in_2);
endmodule

module FullAdder (
  input  in_1,
  input  in_2,
  input  in_3,
  output out_4,
  output out_5
);

  wire and_1_out, and_2_out, xor_1_out;

  xor xor_1 (xor_1_out, in_1, in_2);
  xor xor_2 (out_4, xor_1_out, in_3);
  and and_1 (and_1_out, xor_1_out, in_3);
  and and_2 (and_2_out, in_1, in_2);
  or or_1 (out_5, and_1_out, and_2_out);
endmodule

module _2bitAdder (
  input  in_1,
  input  in_2,
  input  in_3,
  input  in_4,
  output out_5,
  output out_6,
  output out_7
);

  wire halfadder_1_out_4;

  FullAdder fulladder_1 (.in_1(halfadder_1_out_4), .in_2(in_1), .in_3(in_2), .out_4(out_5), .out_5(out_7));
  HalfAdder halfadder_1 (.in_1(in_4), .in_2(in_3), .out_3(out_6), .out_4(halfadder_1_out_4));
endmodule

module _2sComplementInverter (
  input  in_1,
  input  in_2,
  input  in_3,
  output out_4,
  output out_5,
  output out_6,
  output out_7
);

  wire halfadder_1_out_4, halfadder_3_out_4, not_1_out, not_2_out, not_3_out;

  not not_1 (not_1_out, in_1);
  not not_2 (not_2_out, in_2);
  HalfAdder halfadder_1 (.in_1(halfadder_3_out_4), .in_2(not_2_out), .out_3(out_7), .out_4(halfadder_1_out_4));
  HalfAdder halfadder_2 (.in_1(halfadder_1_out_4), .in_2(not_1_out), .out_3(out_5), .out_4(out_4));
  not not_3 (not_3_out, in_3);
  HalfAdder halfadder_3 (.in_1(1'b1), .in_2(not_3_out), .out_3(out_6), .out_4(halfadder_3_out_4));
endmodule

module ControlledInverter (
  input  in_1,
  input  in_2,
  input  in_3,
  input  in_4,
  output out_5,
  output out_6,
  output out_7,
  output out_8
);

  wire halfadder_2_out_4, halfadder_3_out_4, xor_1_out, xor_2_out, xor_3_out;

  xor xor_1 (xor_1_out, in_4, in_1);
  HalfAdder halfadder_1 (.in_1(halfadder_2_out_4), .in_2(xor_1_out), .out_3(out_6), .out_4(out_5));
  xor xor_2 (xor_2_out, in_4, in_2);
  HalfAdder halfadder_2 (.in_1(halfadder_3_out_4), .in_2(xor_2_out), .out_3(out_7), .out_4(halfadder_2_out_4));
  xor xor_3 (xor_3_out, in_4, in_3);
  HalfAdder halfadder_3 (.in_1(in_4), .in_2(xor_3_out), .out_3(out_8), .out_4(halfadder_3_out_4));
endmodule

module _2LineMultiplexer (
  input  in_1,
  input  in_2,
  input  in_3,
  output out_4
);

  wire _0_out, _1_out, not_1_out;

  not not_1 (not_1_out, in_1);
  and _0 (_0_out, not_1_out, in_2);
  and _1 (_1_out, in_1, in_3);
  or or_1 (out_4, _0_out, _1_out);
endmodule

module _4LineMultiplexer (
  input  in_1,
  input  in_2,
  input  in_3,
  input  in_4,
  input  in_5,
  input  in_6,
  output out_7
);

  wire _00_out, _01_out, _10_out, _11_out, not_1_out, not_2_out, not_3_out, not_4_out;

  not not_1 (not_1_out, in_2);
  not not_2 (not_2_out, in_1);
  not not_3 (not_3_out, in_1);
  not not_4 (not_4_out, in_2);
  and _00 (_00_out, not_1_out, not_2_out, in_3);
  and _01 (_01_out, not_3_out, in_2, in_4);
  and _10 (_10_out, in_1, not_4_out, in_5);
  and _11 (_11_out, in_1, in_2, in_6);
  or or_1 (out_7, _00_out, _01_out, _10_out, _11_out);
endmodule

module ALU (
  input  in_1,
  input  in_2,
  input  in_3,
  input  in_4,
  input  in_5,
  output out_6,
  output out_7
);

  wire and_1_out, fulladder_1_out_4, n2linemultiplexer_1_out_4, not_1_out, or_1_out;

  _2LineMultiplexer u_2linemultiplexer_1 (
    .in_2(in_5), .in_3(not_1_out), .out_4(n2linemultiplexer_1_out_4), .in_1(in_3));
  not not_1 (not_1_out, in_5);
  and and_1 (and_1_out, in_4, in_5);
  or or_1 (or_1_out, in_4, in_5);
  FullAdder fulladder_1 (
    .in_1(in_4), .in_2(in_1), .in_3(n2linemultiplexer_1_out_4), .out_4(fulladder_1_out_4), .out_5(out_7));
  _4LineMultiplexer u_4linemultiplexer_1 (
    .in_3(and_1_out), .in_4(or_1_out), .in_5(fulladder_1_out_4), .in_6(fulladder_1_out_4), .out_7(out_6),
    .in_1(in_2), .in_2(in_3));
endmodule
