// Logisim project ODD&EVEN FUNCTION.circ as structural Verilog: 3 circuits, main circuit main
module main (
  input  in_1,
  input  in_2,
  input  in_3,
  input  in_4,
  output out_5,
  output out_6,
  output out_7,
  output out_8,
  output out_9
);

  wire odd_1_out_5;

  ODD odd_1 (.in_1(in_4), .in_2(in_3), .in_3(in_2), .in_4(in_1), .out_5(odd_1_out_5));
  EVEN even_1 (.in_1(in_4), .in_2(in_3), .in_3(in_2), .in_4(in_1), .in_5(odd_1_out_5), .out_6(out_9));

  assign out_5 = in_1;
  assign out_6 = in_2;
  assign out_7 = in_3;
  assign out_8 = in_4;
endmodule

module ODD (
  input  in_1,
  input  in_2,
  input  in_3,
  input  in_4,
  output out_5
);

  wire xor_1_out, xor_2_out;

  xor xor_1 (xor_1_out, in_1, in_2);
  xor xor_2 (xor_2_out, xor_1_out, in_3);
  xor xor_3 (out_5, xor_2_out, in_4);
endmodule

module EVEN (
  input  in_1,
  input  in_2,
  input  in_3,
  input  in_4,
  input  in_5,
  output out_6
);

  wire xor_1_out, xor_2_out, xor_3_out, xor_4_out;

  xor xor_1 (xor_1_out, in_1, in_2);
  xor xor_2 (xor_2_out, xor_1_out, in_3);
  xor xor_3 (xor_3_out, xor_2_out, in_4);
  xor xor_4 (xor_4_out, xor_3_out, in_5);
  not not_1 (out_6, xor_4_out);
endmodule
