// Logisim project Comparator - GreaterThan.circ as structural Verilog: 1 circuit, main circuit main
module main (
  input  A,
  input  B,
  output A___B
);

  wire not_1_out;

  not not_1 (not_1_out, B);
  and and_1 (A___B, A, A, not_1_out);
endmodule
