// Logisim project Comparator - LessThan.circ as structural Verilog: 1 circuit, main circuit main
module main (
  input  A,
  input  B,
  output A___B
);

  wire not_1_out;

  not not_1 (not_1_out, A);
  and and_1 (A___B, not_1_out, B);
endmodule
