// Logisim project Decoder - 1x2.circ as structural Verilog: 1 circuit, main circuit main
module main (
  input  X,
  output line_0,
  output line_1
);

  not not_1 (line_0, X);

  assign line_1 = X;
endmodule
