// Logisim project Decoder - 2x4.circ as structural Verilog: 1 circuit, main circuit main
module main (
  input  X,
  input  Y,
  output line_0,
  output line_1,
  output line_2,
  output line_3
);

  wire not_1_out, not_2_out, not_3_out, not_4_out;

  not not_1 (not_1_out, X);
  not not_2 (not_2_out, Y);
  not not_3 (not_3_out, X);
  not not_4 (not_4_out, Y);
  and _00 (line_0, not_1_out, not_2_out);
  and _01 (line_1, not_3_out, Y);
  and _10 (line_2, X, not_4_out);
  and _11 (line_3, X, Y);
endmodule
