// Logisim project Decoder - 3x8.circ as structural Verilog: 1 circuit, main circuit main
module main (
  input  X,
  input  Y,
  input  Z,
  output line_0,
  output line_1,
  output line_2,
  output line_3,
  output line_4,
  output line_5,
  output line_6,
  output line_7
);

  wire not_1_out, not_2_out, not_3_out, not_4_out, not_5_out, not_6_out, not_7_out, not_8_out, not_9_out,
       not_10_out, not_11_out, not_12_out;

  not not_1 (not_1_out, X);
  not not_2 (not_2_out, Y);
  not not_3 (not_3_out, Z);
  not not_4 (not_4_out, X);
  not not_5 (not_5_out, Y);
  not not_6 (not_6_out, X);
  not not_7 (not_7_out, Z);
  not not_8 (not_8_out, X);
  not not_9 (not_9_out, Y);
  not not_10 (not_10_out, Z);
  not not_11 (not_11_out, Y);
  not not_12 (not_12_out, Z);
  and _000 (line_0, not_1_out, not_2_out, not_3_out);
  and _001 (line_1, not_4_out, not_5_out, Z);
  and _010 (line_2, not_6_out, not_6_out, Y, not_7_out);
  and _011 (line_3, not_8_out, Y, Z);
  and _100 (line_4, X, not_9_out, not_10_out);
  and _101 (line_5, X, not_11_out, Z);
  and _110 (line_6, X, Y, not_12_out);
  and _111 (line_7, X, Y, Z);
endmodule
