// Logisim project Encoder - 4x2 priority with validation.circ as structural Verilog: 1 circuit, main circuit main
module main (
  input  line_1,
  input  line_1_2,
  input  line_2,
  input  line_3,
  output X,
  output Y,
  output Validation
);

  wire and_1_out, not_1_out;

  not not_1 (not_1_out, line_2);
  and and_1 (and_1_out, line_1_2, not_1_out);
  buf or_1 (X, line_3);  // OR_Gate
  or or_2 (Y, and_1_out, line_3);
  or or_3 (Validation, line_1, line_1_2, line_2, line_3);
endmodule
