// Logisim project Encoder - 4x2.circ as structural Verilog: 1 circuit, main circuit main
module main (
  input  line_0,
  input  line_1,
  input  line_2,
  input  line_3,
  output X,
  output Y
);

  or or_1 (X, line_2, line_3);
  or or_2 (Y, line_1, line_3);
endmodule
