// Logisim project Mux - 2 to 1.circ as structural Verilog: 1 circuit, main circuit main
module main (
  input  in_1,
  input  in_2,
  input  in_3,
  output out_4
);

  wire _0_out, _1_out, not_1_out;

  not not_1 (not_1_out, in_3);
  and _0 (_0_out, in_1, not_1_out);
  and _1 (_1_out, in_2, in_3);
  or or_1 (out_4, _0_out, _1_out);
endmodule
