// Logisim project Mux - 4 to 2.circ as structural Verilog: 1 circuit, main circuit main
module main (
  input  in_1,
  input  in_2,
  input  in_3,
  input  in_4,
  input  in_5,
  input  in_6,
  output out_7
);

  wire _00_out, _01_out, _10_out, _11_out, not_1_out, not_2_out, not_3_out, not_4_out;

  not not_1 (not_1_out, in_5);
  not not_2 (not_2_out, in_6);
  not not_3 (not_3_out, in_5);
  not not_4 (not_4_out, in_6);
  and _00 (_00_out, in_1, not_1_out, not_2_out);
  and _01 (_01_out, in_2, not_3_out, in_6);
  and _10 (_10_out, in_3, in_5, not_4_out);
  and _11 (_11_out, in_4, in_5, in_6);
  or or_1 (out_7, _00_out, _01_out, _10_out, _11_out);
endmodule
